// Logisim project computer_8bits.circ as structural Verilog: 7 circuits, main circuit Processor
module Processor (
  input  Halt,
  input  IA,
  input  OA,
  input  CA,
  input  SE,
  input  OE,
  input  IB,
  input  OB,
  input  CB,
  input  IM,
  input  CM,
  input  in_12,
  input  in_13,
  input  in_14,
  input  in_15,
  input  in_16,
  input  in_17,
  input  in_18,
  input  in_19,
  input  in_20,
  input  CI,
  input  PE,
  input  PJ,
  input  II,
  input  OI,
  input  CI_2
);

  wire alu_8_bits_1_co, alu_8_bits_1_s0, alu_8_bits_1_s1, alu_8_bits_1_s2, alu_8_bits_1_s3, alu_8_bits_1_s4,
       alu_8_bits_1_s5, alu_8_bits_1_s6, alu_8_bits_1_s7, and_1_out, clock_1_out, counter_8_bits_1_o0,
       counter_8_bits_1_o1, counter_8_bits_1_o2, counter_8_bits_1_o3, counter_8_bits_1_o4,
       counter_8_bits_1_o5, counter_8_bits_1_o6, counter_8_bits_1_o7, register_8_bits_1_b0,
       register_8_bits_1_b1, register_8_bits_1_b2, register_8_bits_1_b3, register_8_bits_1_b4,
       register_8_bits_1_b5, register_8_bits_1_b6, register_8_bits_1_b7, register_8_bits_1_o0,
       register_8_bits_1_o1, register_8_bits_1_o2, register_8_bits_1_o3, register_8_bits_1_o4,
       register_8_bits_1_o5, register_8_bits_1_o6, register_8_bits_1_o7, register_8_bits_2_b0,
       register_8_bits_2_b1, register_8_bits_2_b2, register_8_bits_2_b3, register_8_bits_2_b4,
       register_8_bits_2_b5, register_8_bits_2_b6, register_8_bits_2_b7, register_8_bits_2_o0,
       register_8_bits_2_o1, register_8_bits_2_o2, register_8_bits_2_o3, register_8_bits_2_o4,
       register_8_bits_2_o5, register_8_bits_2_o6, register_8_bits_2_o7, register_8_bits_3_b0,
       register_8_bits_3_b1, register_8_bits_3_b2, register_8_bits_3_b3, register_8_bits_3_b4,
       register_8_bits_3_b5, register_8_bits_3_b6, register_8_bits_3_b7, register_8_bits_4_b0,
       register_8_bits_4_b1, register_8_bits_4_b2, register_8_bits_4_b3, register_8_bits_4_b4,
       register_8_bits_4_b5, register_8_bits_4_b6, register_8_bits_4_b7, reverser_8_bits_1_s0,
       reverser_8_bits_1_s1, reverser_8_bits_1_s2, reverser_8_bits_1_s3, reverser_8_bits_1_s4,
       reverser_8_bits_1_s5, reverser_8_bits_1_s6, reverser_8_bits_1_s7;

  Clock clock_1 (.out(clock_1_out));
  and and_1 (and_1_out, clock_1_out, ~Halt);  // AND_Gate
  DotMatrix #(.inputtype("row"), .matrixcols(1), .matrixrows(8), .dotshape("circle")) dotmatrix_1 (
    .row0(register_8_bits_1_o7), .row1(register_8_bits_1_o6), .row2(register_8_bits_1_o5),
    .row3(register_8_bits_1_o4), .row4(register_8_bits_1_o3), .row5(register_8_bits_1_o2),
    .row6(register_8_bits_1_o1));  // open: row7
  DotMatrix #(.matrixcols(8), .matrixrows(1), .dotshape("circle")) dotmatrix_2 (
    .col0(register_8_bits_1_b7), .col1(register_8_bits_1_b6), .col2(register_8_bits_1_b5),
    .col3(register_8_bits_1_b4), .col4(register_8_bits_1_b3), .col5(register_8_bits_1_b2),
    .col6(register_8_bits_1_b1), .col7(register_8_bits_1_b0));
  DotMatrix #(.matrixcols(8), .matrixrows(1), .dotshape("circle")) dotmatrix_3 (
    .col0(counter_8_bits_1_o7), .col1(counter_8_bits_1_o6), .col2(counter_8_bits_1_o5),
    .col3(counter_8_bits_1_o4), .col4(counter_8_bits_1_o3), .col5(counter_8_bits_1_o2),
    .col6(counter_8_bits_1_o1), .col7(counter_8_bits_1_o0));
  Register_8_bits register_8_bits_1 (
    .I7(register_8_bits_1_o7), .I6(register_8_bits_1_o6), .I5(register_8_bits_1_o5),
    .I4(register_8_bits_1_o4), .I3(register_8_bits_1_o3), .I2(register_8_bits_1_o2),
    .I1(register_8_bits_1_o1), .I0(register_8_bits_1_o0), .O7(register_8_bits_1_o7),
    .O6(register_8_bits_1_o6), .O5(register_8_bits_1_o5), .O4(register_8_bits_1_o4),
    .O3(register_8_bits_1_o3), .O2(register_8_bits_1_o2), .O1(register_8_bits_1_o1),
    .O0(register_8_bits_1_o0), .Clock(and_1_out), .Load(IA), .Clear(CA), .Enable(OA),
    .B7(register_8_bits_1_b7), .B6(register_8_bits_1_b6), .B5(register_8_bits_1_b5),
    .B4(register_8_bits_1_b4), .B3(register_8_bits_1_b3), .B2(register_8_bits_1_b2),
    .B1(register_8_bits_1_b1), .B0(register_8_bits_1_b0));
  Counter_8_bits counter_8_bits_1 (
    .Enabled(PE), .Reset(CI), .Write(PJ), .Clock(and_1_out), .O7(counter_8_bits_1_o7),
    .O6(counter_8_bits_1_o6), .O5(counter_8_bits_1_o5), .O4(counter_8_bits_1_o4), .O3(counter_8_bits_1_o3),
    .O2(counter_8_bits_1_o2), .O1(counter_8_bits_1_o1), .O0(counter_8_bits_1_o0), .I7(register_8_bits_1_o7),
    .I6(register_8_bits_1_o6), .I5(register_8_bits_1_o5), .I4(register_8_bits_1_o4),
    .I3(register_8_bits_1_o3), .I2(register_8_bits_1_o2), .I1(register_8_bits_1_o1), .I0(register_8_bits_1_o0));
  LED led_1 (.in(alu_8_bits_1_co));
  DotMatrix #(.matrixcols(8), .matrixrows(1), .dotshape("circle")) dotmatrix_4 (
    .col0(alu_8_bits_1_s7), .col1(alu_8_bits_1_s6), .col2(alu_8_bits_1_s5), .col3(alu_8_bits_1_s4),
    .col4(alu_8_bits_1_s3), .col5(alu_8_bits_1_s2), .col6(alu_8_bits_1_s1), .col7(alu_8_bits_1_s0));
  ALU_8_bits alu_8_bits_1 (
    .E7(register_8_bits_1_o7), .E6(register_8_bits_1_o6), .E5(register_8_bits_1_o5),
    .E4(register_8_bits_1_o4), .E2(register_8_bits_1_o2), .E1(register_8_bits_1_o1),
    .E0(register_8_bits_1_o0), .Su(SE), .A7(register_8_bits_1_b7), .A6(register_8_bits_1_b6),
    .A5(register_8_bits_1_b5), .A4(register_8_bits_1_b4), .A3(register_8_bits_1_b3),
    .A2(register_8_bits_1_b2), .A1(register_8_bits_1_b1), .A0(register_8_bits_1_b0), .CO(alu_8_bits_1_co),
    .S7(alu_8_bits_1_s7), .S6(alu_8_bits_1_s6), .S5(alu_8_bits_1_s5), .S4(alu_8_bits_1_s4),
    .S3(alu_8_bits_1_s3), .S2(alu_8_bits_1_s2), .S1(alu_8_bits_1_s1), .S0(alu_8_bits_1_s0), .En(OE),
    .B7(register_8_bits_3_b7), .B6(register_8_bits_3_b6), .B5(register_8_bits_3_b5),
    .B4(register_8_bits_3_b4), .B3(register_8_bits_3_b3), .B2(register_8_bits_3_b2),
    .B1(register_8_bits_3_b1), .B0(register_8_bits_3_b0), .E3(register_8_bits_1_o3));
  DotMatrix #(.matrixcols(8), .matrixrows(1), .dotshape("circle")) dotmatrix_5 (
    .col0(register_8_bits_3_b7), .col1(register_8_bits_3_b6), .col2(register_8_bits_3_b5),
    .col3(register_8_bits_3_b4), .col4(register_8_bits_3_b3), .col5(register_8_bits_3_b2),
    .col6(register_8_bits_3_b1), .col7(register_8_bits_3_b0));
  DotMatrix #(.matrixcols(8), .matrixrows(1), .dotshape("circle")) dotmatrix_6 (
    .col0(reverser_8_bits_1_s0), .col1(reverser_8_bits_1_s1), .col2(reverser_8_bits_1_s2),
    .col3(reverser_8_bits_1_s3), .col4(reverser_8_bits_1_s4), .col5(reverser_8_bits_1_s5),
    .col6(reverser_8_bits_1_s6), .col7(reverser_8_bits_1_s7));
  Reverser_8_bits reverser_8_bits_1 (
    .S0(reverser_8_bits_1_s0), .S1(reverser_8_bits_1_s1), .S2(reverser_8_bits_1_s2),
    .S3(reverser_8_bits_1_s3), .S4(reverser_8_bits_1_s4), .S5(reverser_8_bits_1_s5),
    .S6(reverser_8_bits_1_s6), .S7(reverser_8_bits_1_s7), .E7(register_8_bits_2_b0),
    .E6(register_8_bits_2_b1), .E5(register_8_bits_2_b2), .E4(register_8_bits_2_b3),
    .E3(register_8_bits_2_b4), .E2(register_8_bits_2_b5), .E1(register_8_bits_2_b6), .E0(register_8_bits_2_b7));
  DotMatrix #(.inputtype("row"), .matrixcols(1), .matrixrows(8), .dotshape("circle")) dotmatrix_7 (
    .row0(register_8_bits_2_o0), .row1(register_8_bits_2_o1), .row2(register_8_bits_2_o2),
    .row3(register_8_bits_2_o3), .row4(register_8_bits_2_o4), .row5(register_8_bits_2_o5),
    .row6(register_8_bits_2_o6), .row7(register_8_bits_2_o7));
  Register_8_bits register_8_bits_2 (
    .I7(register_8_bits_1_o7), .I6(register_8_bits_1_o6), .I5(register_8_bits_1_o5),
    .I4(register_8_bits_1_o4), .I3(register_8_bits_1_o3), .I2(register_8_bits_1_o2),
    .I1(register_8_bits_1_o1), .I0(register_8_bits_1_o0), .O7(register_8_bits_2_o7),
    .O6(register_8_bits_2_o6), .O5(register_8_bits_2_o5), .O4(register_8_bits_2_o4),
    .O3(register_8_bits_2_o3), .O2(register_8_bits_2_o2), .O1(register_8_bits_2_o1),
    .O0(register_8_bits_2_o0), .Clock(and_1_out), .Load(II), .Clear(CI_2), .Enable(OI),
    .B7(register_8_bits_2_b7), .B6(register_8_bits_2_b6), .B5(register_8_bits_2_b5),
    .B4(register_8_bits_2_b4), .B3(register_8_bits_2_b3), .B2(register_8_bits_2_b2),
    .B1(register_8_bits_2_b1), .B0(register_8_bits_2_b0));
  Register_8_bits register_8_bits_3 (
    .I7(register_8_bits_1_o7), .I6(register_8_bits_1_o6), .I5(register_8_bits_1_o5),
    .I4(register_8_bits_1_o4), .I3(register_8_bits_1_o3), .I2(register_8_bits_1_o2),
    .I1(register_8_bits_1_o1), .I0(register_8_bits_1_o0), .O7(register_8_bits_1_o7),
    .O6(register_8_bits_1_o6), .O5(register_8_bits_1_o5), .O4(register_8_bits_1_o4),
    .O3(register_8_bits_1_o3), .O2(register_8_bits_1_o2), .O1(register_8_bits_1_o1),
    .O0(register_8_bits_1_o0), .Clock(and_1_out), .Load(IB), .Clear(CB), .Enable(OB),
    .B7(register_8_bits_3_b7), .B6(register_8_bits_3_b6), .B5(register_8_bits_3_b5),
    .B4(register_8_bits_3_b4), .B3(register_8_bits_3_b3), .B2(register_8_bits_3_b2),
    .B1(register_8_bits_3_b1), .B0(register_8_bits_3_b0));
  DotMatrix #(.matrixcols(8), .matrixrows(1), .dotshape("circle")) dotmatrix_8 (
    .col0(register_8_bits_4_b7), .col1(register_8_bits_4_b6), .col2(register_8_bits_4_b5),
    .col3(register_8_bits_4_b4), .col4(register_8_bits_4_b3), .col5(register_8_bits_4_b2),
    .col6(register_8_bits_4_b1), .col7(register_8_bits_4_b0));
  assign register_8_bits_1_o7 = in_12 ? in_13 : 1'bz;  // Controlled_Buffer controlled_buffer_1
  assign register_8_bits_1_o6 = in_12 ? in_14 : 1'bz;  // Controlled_Buffer controlled_buffer_2
  assign register_8_bits_1_o5 = in_12 ? in_15 : 1'bz;  // Controlled_Buffer controlled_buffer_3
  assign register_8_bits_1_o4 = in_12 ? in_16 : 1'bz;  // Controlled_Buffer controlled_buffer_4
  assign register_8_bits_1_o3 = in_12 ? in_17 : 1'bz;  // Controlled_Buffer controlled_buffer_5
  assign register_8_bits_1_o2 = in_12 ? in_18 : 1'bz;  // Controlled_Buffer controlled_buffer_6
  assign register_8_bits_1_o1 = in_12 ? in_19 : 1'bz;  // Controlled_Buffer controlled_buffer_7
  assign register_8_bits_1_o0 = in_12 ? in_20 : 1'bz;  // Controlled_Buffer controlled_buffer_8
  Register_8_bits register_8_bits_4 (
    .I7(register_8_bits_1_o7), .I6(register_8_bits_1_o6), .I5(register_8_bits_1_o5),
    .I4(register_8_bits_1_o4), .I3(register_8_bits_1_o3), .I2(register_8_bits_1_o2),
    .I1(register_8_bits_1_o1), .I0(register_8_bits_1_o0), .Clock(and_1_out), .Load(IM), .Clear(CM),
    .B7(register_8_bits_4_b7), .B6(register_8_bits_4_b6), .B5(register_8_bits_4_b5),
    .B4(register_8_bits_4_b4), .B3(register_8_bits_4_b3), .B2(register_8_bits_4_b2),
    .B1(register_8_bits_4_b1), .B0(register_8_bits_4_b0));  // open: O7, O6, O5, O4, O3, O2, O1, O0, Enable

  // Notes on the sheet:
  //   Register A
  //   PC Register
  //   ALU
  //   Register B
  //   Instruction
  //   Register
  //   Memory
  //   Register
endmodule

module Register_8_bits (
  input  Clock,
  input  Load,
  input  Clear,
  input  Enable,
  input  I7,
  input  I6,
  input  I5,
  input  I4,
  input  I3,
  input  I2,
  input  I1,
  input  I0,
  output B7,
  output B6,
  output B5,
  output B4,
  output B3,
  output B2,
  output B1,
  output B0,
  output O7,
  output O6,
  output O5,
  output O4,
  output O3,
  output O2,
  output O1,
  output O0
);

  Register #(.width(1)) register_1 (.D(I7), .en(Load), .Q(B7), .clk(Clock), .clr(Clear));
  Register #(.width(1)) register_2 (.D(I6), .en(Load), .Q(B6), .clk(Clock), .clr(Clear));
  Register #(.width(1)) register_3 (.D(I5), .en(Load), .Q(B5), .clk(Clock), .clr(Clear));
  Register #(.width(1)) register_4 (.D(I4), .en(Load), .Q(B4), .clk(Clock), .clr(Clear));
  Register #(.width(1)) register_5 (.D(I3), .en(Load), .Q(B3), .clk(Clock), .clr(Clear));
  Register #(.width(1)) register_6 (.D(I2), .en(Load), .Q(B2), .clk(Clock), .clr(Clear));
  Register #(.width(1)) register_7 (.D(I1), .en(Load), .Q(B1), .clk(Clock), .clr(Clear));
  Register #(.width(1)) register_8 (.D(I0), .en(Load), .Q(B0), .clk(Clock), .clr(Clear));
  assign O7 = Enable ? B7 : 1'bz;  // Controlled_Buffer controlled_buffer_1
  assign O6 = Enable ? B6 : 1'bz;  // Controlled_Buffer controlled_buffer_2
  assign O5 = Enable ? B5 : 1'bz;  // Controlled_Buffer controlled_buffer_3
  assign O4 = Enable ? B4 : 1'bz;  // Controlled_Buffer controlled_buffer_4
  assign O3 = Enable ? B3 : 1'bz;  // Controlled_Buffer controlled_buffer_5
  assign O2 = Enable ? B2 : 1'bz;  // Controlled_Buffer controlled_buffer_6
  assign O1 = Enable ? B1 : 1'bz;  // Controlled_Buffer controlled_buffer_7
  assign O0 = Enable ? B0 : 1'bz;  // Controlled_Buffer controlled_buffer_8
endmodule

module Full_adder (
  input  A,
  input  B,
  input  Ci,
  output E,
  output Co
);

  wire and_1_out, and_2_out, xor_1_out;

  xor xor_1 (xor_1_out, A, B);
  and and_1 (and_1_out, xor_1_out, Ci);
  and and_2 (and_2_out, A, B);
  xor xor_2 (E, xor_1_out, Ci);
  or or_1 (Co, and_1_out, and_2_out);
endmodule

module ALU_8_bits (
  input  Su,
  input  A7,
  input  A6,
  input  A5,
  input  A4,
  input  A3,
  input  A2,
  input  A1,
  input  A0,
  input  En,
  input  B7,
  input  B6,
  input  B5,
  input  B4,
  input  B3,
  input  B2,
  input  B1,
  input  B0,
  output CO,
  output S7,
  output S6,
  output S5,
  output S4,
  output S3,
  output S2,
  output S1,
  output S0,
  output E7,
  output E6,
  output E5,
  output E4,
  output E3,
  output E2,
  output E1,
  output E0
);

  wire full_adder_1_co, full_adder_2_co, full_adder_3_co, full_adder_4_co, full_adder_5_co, full_adder_6_co,
       full_adder_7_co, xor_1_out, xor_2_out, xor_3_out, xor_4_out, xor_5_out, xor_6_out, xor_7_out,
       xor_8_out;

  Full_adder full_adder_1 (.B(xor_8_out), .Ci(Su), .E(S0), .Co(full_adder_1_co), .A(A0));
  Full_adder full_adder_2 (.B(xor_6_out), .Ci(full_adder_1_co), .E(S1), .Co(full_adder_2_co), .A(A1));
  xor xor_1 (xor_1_out, Su, B7);
  Full_adder full_adder_3 (.B(xor_7_out), .Ci(full_adder_2_co), .E(S2), .Co(full_adder_3_co), .A(A2));
  xor xor_2 (xor_2_out, Su, B6);
  xor xor_3 (xor_3_out, Su, B5);
  Full_adder full_adder_4 (.B(xor_4_out), .Ci(full_adder_3_co), .E(S3), .Co(full_adder_4_co), .A(A3));
  xor xor_4 (xor_4_out, Su, B3);
  xor xor_5 (xor_5_out, Su, B4);
  Full_adder full_adder_5 (.B(xor_3_out), .Ci(full_adder_6_co), .E(S5), .Co(full_adder_5_co), .A(A5));
  Full_adder full_adder_6 (.B(xor_5_out), .Ci(full_adder_4_co), .E(S4), .Co(full_adder_6_co), .A(A4));
  xor xor_6 (xor_6_out, Su, B1);
  xor xor_7 (xor_7_out, Su, B2);
  Full_adder full_adder_7 (.B(xor_2_out), .Ci(full_adder_5_co), .E(S6), .Co(full_adder_7_co), .A(A6));
  xor xor_8 (xor_8_out, Su, B0);
  Full_adder full_adder_8 (.B(xor_1_out), .Ci(full_adder_7_co), .E(S7), .Co(CO), .A(A7));
  assign E7 = En ? S7 : 1'bz;  // Controlled_Buffer controlled_buffer_1
  assign E6 = En ? S6 : 1'bz;  // Controlled_Buffer controlled_buffer_2
  assign E5 = En ? S5 : 1'bz;  // Controlled_Buffer controlled_buffer_3
  assign E4 = En ? S4 : 1'bz;  // Controlled_Buffer controlled_buffer_4
  assign E3 = En ? S3 : 1'bz;  // Controlled_Buffer controlled_buffer_5
  assign E2 = En ? S2 : 1'bz;  // Controlled_Buffer controlled_buffer_6
  assign E1 = En ? S1 : 1'bz;  // Controlled_Buffer controlled_buffer_7
  assign E0 = En ? S0 : 1'bz;  // Controlled_Buffer controlled_buffer_8
endmodule

module Reverser_8_bits (
  input  E7,
  input  E6,
  input  E5,
  input  E4,
  input  E3,
  input  E2,
  input  E1,
  input  E0,
  output S0,
  output S1,
  output S2,
  output S3,
  output S4,
  output S5,
  output S6,
  output S7
);


  assign S0 = E0;
  assign S1 = E1;
  assign S2 = E2;
  assign S3 = E3;
  assign S4 = E4;
  assign S5 = E5;
  assign S6 = E6;
  assign S7 = E7;
endmodule

module Grounder_4_bits (
  input  in_1,
  output G3,
  output G2,
  output G1,
  output G0
);

  assign G3 = in_1 ? 1'b0 : 1'bz;  // Controlled_Buffer controlled_buffer_1
  assign G2 = in_1 ? 1'b0 : 1'bz;  // Controlled_Buffer controlled_buffer_2
  assign G1 = in_1 ? 1'b0 : 1'bz;  // Controlled_Buffer controlled_buffer_3
  assign G0 = in_1 ? 1'b0 : 1'bz;  // Controlled_Buffer controlled_buffer_4
endmodule

module Counter_8_bits (
  input  Clock,
  input  Enabled,
  input  Reset,
  input  Write,
  input  I7,
  input  I6,
  input  I5,
  input  I4,
  input  I3,
  input  I2,
  input  I1,
  input  I0,
  output O7,
  output O6,
  output O5,
  output O4,
  output O3,
  output O2,
  output O1,
  output O0
);

  wire and_1_out, and_2_out, and_3_out, and_4_out, and_5_out, and_6_out, and_7_out, and_8_out, and_9_out,
       and_10_out, and_11_out, and_12_out, and_13_out, and_14_out, and_15_out, and_16_out, and_17_out,
       j_k_ff_2_qn, j_k_ff_3_qn, j_k_ff_4_qn, j_k_ff_5_qn, j_k_ff_6_qn, j_k_ff_7_qn, j_k_ff_8_qn, or_1_out,
       or_2_out, or_3_out, or_4_out, or_5_out, or_6_out, or_7_out, or_8_out;

  and and_1 (and_1_out, Reset, Clock);
  J_K_Flip_Flop j_k_ff_1 (
    .J(1'b1), .clk(j_k_ff_2_qn), .K(1'b1), .Q(O7), .preset(and_2_out), .en(Enabled), .reset(or_1_out));  // open: Qn
  or or_1 (or_1_out, and_1_out, and_3_out);
  and and_2 (and_2_out, Write, I7, Clock);
  and and_3 (and_3_out, Write, ~I7, Clock);  // AND_Gate
  J_K_Flip_Flop j_k_ff_2 (
    .J(1'b1), .clk(j_k_ff_3_qn), .K(1'b1), .Q(O6), .Qn(j_k_ff_2_qn), .preset(and_5_out), .en(Enabled),
    .reset(or_2_out));
  or or_2 (or_2_out, and_1_out, and_4_out);
  and and_4 (and_4_out, Write, ~I6, Clock);  // AND_Gate
  and and_5 (and_5_out, Write, I6, Clock);
  J_K_Flip_Flop j_k_ff_3 (
    .J(1'b1), .clk(j_k_ff_4_qn), .K(1'b1), .Q(O5), .Qn(j_k_ff_3_qn), .preset(and_7_out), .en(Enabled),
    .reset(or_3_out));
  or or_3 (or_3_out, and_1_out, and_6_out);
  and and_6 (and_6_out, Write, ~I5, Clock);  // AND_Gate
  and and_7 (and_7_out, Write, I5, Clock);
  J_K_Flip_Flop j_k_ff_4 (
    .J(1'b1), .clk(j_k_ff_5_qn), .K(1'b1), .Q(O4), .Qn(j_k_ff_4_qn), .preset(and_8_out), .en(Enabled),
    .reset(or_4_out));
  or or_4 (or_4_out, and_1_out, and_9_out);
  and and_8 (and_8_out, Write, I4, Clock);
  and and_9 (and_9_out, Write, ~I4, Clock);  // AND_Gate
  J_K_Flip_Flop j_k_ff_5 (
    .J(1'b1), .clk(j_k_ff_6_qn), .K(1'b1), .Q(O3), .Qn(j_k_ff_5_qn), .preset(and_10_out), .en(Enabled),
    .reset(or_5_out));
  or or_5 (or_5_out, and_1_out, and_11_out);
  and and_10 (and_10_out, Write, I3, Clock);
  and and_11 (and_11_out, Write, ~I3, Clock);  // AND_Gate
  J_K_Flip_Flop j_k_ff_6 (
    .J(1'b1), .clk(j_k_ff_7_qn), .K(1'b1), .Q(O2), .Qn(j_k_ff_6_qn), .preset(and_12_out), .en(Enabled),
    .reset(or_6_out));
  or or_6 (or_6_out, and_1_out, and_13_out);
  and and_12 (and_12_out, Write, I2, Clock);
  and and_13 (and_13_out, Write, ~I2, Clock);  // AND_Gate
  J_K_Flip_Flop j_k_ff_7 (
    .J(1'b1), .clk(j_k_ff_8_qn), .K(1'b1), .Q(O1), .Qn(j_k_ff_7_qn), .preset(and_15_out), .en(Enabled),
    .reset(or_7_out));
  or or_7 (or_7_out, and_1_out, and_14_out);
  and and_14 (and_14_out, Write, ~I1, Clock);  // AND_Gate
  and and_15 (and_15_out, Write, I1, Clock);
  J_K_Flip_Flop j_k_ff_8 (
    .J(1'b1), .clk(Clock), .K(1'b1), .Q(O0), .Qn(j_k_ff_8_qn), .preset(and_16_out), .en(Enabled),
    .reset(or_8_out));
  or or_8 (or_8_out, and_1_out, and_17_out);
  and and_16 (and_16_out, Write, I0, Clock);
  and and_17 (and_17_out, Write, ~I0, Clock);  // AND_Gate
endmodule
